# Fritzing sketch Esquema control 3 antenas OLED (saved by Fritzing 0.9.3b)
breadboards: 1

parts:
  Componente1 = Arduino Uno (Rev3)
  Arduino_CNC_Shield_V3_00_1 = Arduino_CNC_V3.00
  M1 = Stepper Motor - Bipolar
  M3 = Stepper Motor - Bipolar
  S1 = Pushbutton [package="[THT]"]
  S2 = Pushbutton [package="[THT]"]
  S3 = Pushbutton [package="[THT]"]
  S4 = Pushbutton [package="[THT]"]
  S5 = Pushbutton [package="[THT]"]
  Yumo-enc1 = YumoE6B2
  D2F1 = D2F-FL Omron Snap Action Limit Switch with Level
  D2F2 = D2F-FL Omron Snap Action Limit Switch with Level
  D2F3 = D2F-FL Omron Snap Action Limit Switch with Level  # not connected
  D2F4 = D2F-FL Omron Snap Action Limit Switch with Level
  D2F5 = D2F-FL Omron Snap Action Limit Switch with Level
  D2F6 = D2F-FL Omron Snap Action Limit Switch with Level  # not connected
  M2 = Stepper Motor - Bipolar
  Grove1 = Grove OLED 128x96

nets:
  N1: Componente1.A0, S2.Pin_1, S2.Pin_2
  N2: Componente1.A1, S1.Pin_1, S1.Pin_2
  N3: Componente1.A2, S3.Pin_1
  N4: Componente1.A3, S4.Pin_1, S4.Pin_2
  N5: Componente1.A4/SDA, Grove1.SDA
  N6: Componente1.A5/SCL, Grove1.SCL
  N7: Componente1.D9_PWM, Yumo-enc1.PHASE_B
  N8: Componente1.D10_PWM/SS, Yumo-enc1.PHASE_A
  N9: Componente1.D11_PWM/MOSI, S5.Pin_1, S5.Pin_2
  N10: Componente1.D12/MISO, D2F2.NO, D2F4.NO, D2F5.NO
  N11: Componente1.D13/SCK, D2F1.NO
  GND: Componente1.GND, Yumo-enc1.GROUND, Grove1.GND
  5V: Componente1.5V, Yumo-enc1.V, Grove1.VCC
  N12: Arduino_CNC_Shield_V3_00_1.X.STEP, Arduino_CNC_Shield_V3_00_1.Y.STEP, Arduino_CNC_Shield_V3_00_1.Z.STEP, Arduino_CNC_Shield_V3_00_1.A.STEP, Arduino_CNC_Shield_V3_00_1.5V
  N13: Arduino_CNC_Shield_V3_00_1.X.DIR, Arduino_CNC_Shield_V3_00_1.Y.DIR, Arduino_CNC_Shield_V3_00_1.Z.DIR, Arduino_CNC_Shield_V3_00_1.A.DIR#10, Arduino_CNC_Shield_V3_00_1.GND
  N14: Arduino_CNC_Shield_V3_00_1.Z(1), Arduino_CNC_Shield_V3_00_1.D12
  N15: Arduino_CNC_Shield_V3_00_1.Z(2), Arduino_CNC_Shield_V3_00_1.A.STP
  N16: Arduino_CNC_Shield_V3_00_1.Z(3), Arduino_CNC_Shield_V3_00_1.A.DIR#27
  N17: Arduino_CNC_Shield_V3_00_1.Z(4), Arduino_CNC_Shield_V3_00_1.D13
  N18: Arduino_CNC_Shield_V3_00_1.X-MTR_'1', M2.C
  N19: Arduino_CNC_Shield_V3_00_1.X-MTR_'2', M2.D
  N20: Arduino_CNC_Shield_V3_00_1.X-MTR_'3', M2.B
  N21: Arduino_CNC_Shield_V3_00_1.X-MTR_'4', M2.A
  N22: Arduino_CNC_Shield_V3_00_1.Z-MTR_'1', Arduino_CNC_Shield_V3_00_1.Z-MTR_'2', Arduino_CNC_Shield_V3_00_1.Z-MTR_'3', M1.C, M1.B, M1.D
  N23: Arduino_CNC_Shield_V3_00_1.Z-MTR_'4', M1.A
  N24: Arduino_CNC_Shield_V3_00_1.Y-MTR_'1', M3.C
  N25: Arduino_CNC_Shield_V3_00_1.Y-MTR_'2', M3.D
  N26: Arduino_CNC_Shield_V3_00_1.Y-MTR_'3', M3.B
  N27: Arduino_CNC_Shield_V3_00_1.Y-MTR_'4', M3.A
  N28: Arduino_CNC_Shield_V3_00_1.A_-_M0_(5V), Arduino_CNC_Shield_V3_00_1.A_-_M1_(5V), Arduino_CNC_Shield_V3_00_1.A_-_M2_(5V)
  N29: Arduino_CNC_Shield_V3_00_1.A-MTR_'1', Arduino_CNC_Shield_V3_00_1.A-MTR_'2', Arduino_CNC_Shield_V3_00_1.A-MTR_'3'
  N30: S4.Pin_3, S4.Pin_4, S5.Pin_4

custom parts:
  Arduino_CNC_V3.00: Protoneer Arduino CNC Shield V3.00 If using Grbl V0.9: The “A” axis can not be used (yet). The “SCL” (Arduino A5) pin is now used for 'Probing' input. The “End Stops Z+ & Z-” (Arduino D11) and “SpnEn” (Arduino D12) have been switched!
  YumoE6B2: Yumo E6B2-C incremental encoder. Resolutions 10 to 4000 pulses per revolution (depending on model number). Power from 5 to 24V (again depending on model). Dia 40mm body 30mm plus 20mm shaft.
  D2F-FL Omron Snap Action Limit Switch with Level: Snap action switch with stainless steel lever.
